# Fritzing sketch diy-clock (saved by Fritzing 0.9.10b)
breadboards: 1

parts:
  Part1 = Arduino Nano (Rev3.0)
  U1 = POT [knob_status=50% power=0.5W package=pot_alpha_rv16af-20]
  SSD1306_OLED = Grove OLED 128x96
  S1_-_RESET = Momentary Switch [package=ksa_sealed_tac_switch]
  S2_-_SINGLE_STEP = Momentary Switch [package=ksa_sealed_tac_switch]
  S3_-_RUN/STOP = Momentary Switch [package=ksa_sealed_tac_switch]
  LED2 = LED - 3mm [color="Red (633nm)" current=0.030 package="3 mm [THT]"]
  R3 = Resistor [tolerance=±5% power=0.25 resistance=10k package=THT]
  R4 = Resistor [tolerance=±5% power=0.25 resistance=1k package=THT]
  R5 = Resistor [tolerance=±5% power=0.25 resistance=10k package=THT]
  R6 = Resistor [tolerance=±5% power=0.25 resistance=10k package=THT]
  Q1 = NPN-Transistor [package="SOT-23 [SMD]"]
  R7 = Resistor [tolerance=±5% power=0.25 resistance=22k package=THT]

nets:
  N1: Part1.D2, S3_-_RUN/STOP.1, R6.Pin_0
  N2: Part1.D3, S2_-_SINGLE_STEP.1, R5.Pin_0
  N3: Part1.D4, S1_-_RESET.1, R3.Pin_0
  N4: Part1.D10, R7.Pin_1
  N5: Part1.A7, U1.S
  N6: Part1.A5, SSD1306_OLED.SCL
  N7: Part1.A4, SSD1306_OLED.SDA
  5V: U1.A, S1_-_RESET.3, S2_-_SINGLE_STEP.3, S3_-_RUN/STOP.3, R4.Pin_1
  GND: U1.E, R3.Pin_1, R5.Pin_1, R6.Pin_1, Q1.2
  N8: LED2.cathode, Q1.1
  N9: LED2.anode, R4.Pin_0
  N10: Q1.0, R7.Pin_0
